# Fritzing sketch MPU (saved by Fritzing 0.9.3b)
breadboards: 1

parts:
  Arduino_UNO = Arduino Uno (Rev3)
  MPU_9250 = 3-Axis Accelerometer Breakout - MMA8452Q

nets:
  N1: Arduino_UNO.A5/SCL, MPU_9250.SCL
  GND: Arduino_UNO.GND, MPU_9250.GND
  N2: Arduino_UNO.A4/SDA, MPU_9250.SDA
  3V3: Arduino_UNO.3V3, MPU_9250.3.3V
