# Fritzing sketch Prototyp_1 (saved by Fritzing 0.9.3b)
breadboards: 1

parts:
  Atmega328p = DIP - 28 pins [chip_label=IC package="DIP (Dual Inline) [THT]"]
  XTAL1 = Crystal [frequency="16 Mhz" package=THT]
  22_pf = Capacitor [package=cap-pth-small2]
  22_pf_2 = Capacitor [package=cap-pth-small2]
  MPU_9250 = Triple Axis Gyro Breakout ITG-3200
  4_7k_Ohm = 220 Ω Resistor [package=THT]
  4_7k_Ohm_2 = 220 Ω Resistor [package=THT]
  SSD1306_128x64 = Grove OLED 128x96
  Battery_holder = Battery Holders [package=battcom_20mm_pth]

nets:
  N1: Atmega328p.GND#7, 22_pf.2, 22_pf_2.2
  N2: Atmega328p.Crystal#8, XTAL1.pin_0, 22_pf.1
  N3: Atmega328p.Crystal#9, XTAL1.pin_1, 22_pf_2.1
  VCC: Atmega328p.AVCC, MPU_9250.VCC, MPU_9250.SDA, MPU_9250.SCL, 4_7k_Ohm.Pin_1, 4_7k_Ohm_2.Pin_1, SSD1306_128x64.VCC, SSD1306_128x64.SDA, SSD1306_128x64.SCL, Battery_holder.+
  GND: Atmega328p.GND#21, MPU_9250.GND, SSD1306_128x64.GND, Battery_holder.-
  N4: Atmega328p.A_4_(SDA), 4_7k_Ohm_2.Vibration_sensor_meas
  N5: Atmega328p.A_5_(SCL), 4_7k_Ohm.Vibration_sensor_meas

custom parts:
  DIP - 28 pins: A DIP stand-in part for whatever IC you want. With 28 pins on a 300mil dual inline package (DIP) footprint.
  220 Ω Resistor: A generic resistor (0.25W)
