# Fritzing sketch Uppvisningsprototyp (saved by Fritzing 0.9.3b)
breadboards: 1

parts:
  Atmega328p = IC, DIP package, 28 pins [chip_label=IC]
  MPU-9250 = 3-Axis Accelerometer Breakout - MMA8452Q
  LED1 = LED - 5mm [color="Red (633nm)" package="5 mm [THT]"]
  R1 = Resistor [tolerance=±5% resistance=220 package=THT]
  R2 = Resistor [tolerance=±5% resistance=4.7k package=THT]
  R3 = Resistor [tolerance=±5% resistance=4.7k package=THT]
  R4 = Resistor [tolerance=±5% resistance=560 package=THT]

nets:
  N1: Atmega328p.pin7, R2.Pin_1, R3.Pin_1, R4.Pin_0
  N2: Atmega328p.pin8, MPU-9250.GND, R1.Pin_1
  N3: Atmega328p.pin14, LED1.anode
  N4: Atmega328p.pin27, MPU-9250.SDA, R3.Pin_0
  N5: Atmega328p.pin28, MPU-9250.SCL, R2.Pin_0
  N6: MPU-9250.3.3V, R4.Pin_1
