# Fritzing sketch Kopplingsschema_MEAS (saved by Fritzing 0.9.3b)
breadboards: 1

parts:
  Part1 = Arduino Uno (Rev3)
  Vibration_sensor = 220 Ω Resistor [package=THT]
  Resistor = Resistor [tolerance=±5% resistance=1M package=THT]

nets:
  N1: Part1.A0, Vibration_sensor.Vibration_sensor_meas, Resistor.Pin_0
  N2: Part1.GND, Vibration_sensor.Pin_1, Resistor.Pin_1

custom parts:
  220 Ω Resistor: A generic resistor (0.25W)
