# Fritzing sketch Kopplingsschema_MPU (saved by Fritzing 0.9.3b)
breadboards: 1

parts:
  Part1 = Arduino Uno (Rev3)
  3-Axis_Accelerometer1 = 3-Axis Accelerometer Breakout - MMA8452Q

nets:
  N1: Part1.A5/SCL, 3-Axis_Accelerometer1.SCL
  GND: Part1.GND, 3-Axis_Accelerometer1.GND
  N2: Part1.A4/SDA, 3-Axis_Accelerometer1.SDA
  3V3: Part1.3V3, 3-Axis_Accelerometer1.3.3V
