# Fritzing sketch Kopplingsschema_MPU_5V-2.9V (saved by Fritzing 0.9.3b)
breadboards: 1

parts:
  Part1 = Arduino Uno (Rev3)
  3-Axis_Accelerometer1 = 3-Axis Accelerometer Breakout - MMA8452Q
  Resistor = Resistor [tolerance=±5% resistance=560 package="0402 [SMD]"]

nets:
  GND: Part1.GND, 3-Axis_Accelerometer1.GND
  N1: Part1.A4/SDA, 3-Axis_Accelerometer1.SDA
  N2: Part1.A5/SCL, 3-Axis_Accelerometer1.SCL
  N3: Part1.5V, Resistor.Pin_1
  N4: 3-Axis_Accelerometer1.3.3V, Resistor.Pin_0
