# Fritzing sketch Kopplingsschema_MPU_OLED (saved by Fritzing 0.9.3b)
breadboards: 1

parts:
  Part2 = Arduino Uno (Rev3) - ICSP
  Oled_display = Grove OLED 128x96
  3-Axis_Accelerometer1 = 3-Axis Accelerometer Breakout - MMA8452Q

nets:
  N1: Part2.A5/SCL, Oled_display.SCL, 3-Axis_Accelerometer1.SCL
  N2: Part2.ICSP_MISO, Oled_display.SDA, 3-Axis_Accelerometer1.SDA
  GND: Part2.GND, Oled_display.GND, 3-Axis_Accelerometer1.GND
  3V3: Part2.3V3, Oled_display.VCC, 3-Axis_Accelerometer1.3.3V
